# Fritzing sketch FingerPrintDoor (saved by Fritzing 0.9.3b)

parts:
  Part1 = Arduino Uno (Rev3)
  fingerprint = female pin header, 4 pins [form="♀ (female)"]
  J1 = Basic Servo
  Part2 = 24 NeoPixel Ring [part_number=1586]
  S1 = Pushbutton [package="[THT]"]
  S2 = Pushbutton [package="[THT]"]

nets:
  N1: Part1.D8, S2.Pin_2
  N2: Part1.D9_PWM, J1.pulse
  N3: Part1.D10_PWM/SS, S1.Pin_1, S1.Pin_2
  GND: Part1.GND, fingerprint.pin2, J1.gnd, Part2.GND, S1.Pin_4, S2.Pin_3, S2.Pin_4
  N4: Part1.D2, fingerprint.pin3
  N5: Part1.D3_PWM, fingerprint.pin4
  N6: Part1.D6_PWM, Part2.IN
  5V: Part1.5V, fingerprint.pin1, J1.vcc, Part2.VDD

notes:
  + - tx rx

custom parts:
  24 NeoPixel Ring: 24 ultra bright smart LED NeoPixels are arranged in a circle with 2.6" (66mm) outer diameter. The rings are 'chainable' - connect the output pin of one to the input pin of another. Use only one microcontroller pin to control as many as you can chain together! Each LED is addressable as the driver chip is inside the LED. Each one has ~18mA constant current drive so the color will be very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
